# Fritzing sketch IR_Climate (saved by Fritzing 1.0.5)
breadboards: 1

parts:
  Mod1 = Amica NodeMCU DEVKIT 1.0
  LED1 = LED - 3mm [color="Red (633nm)" current=0.030A package="3 mm [THT]"]
  Q1 = TRANSISTOR_NPN [package=to-92]
  U1 = TMP36 [package=to-92]
  R1 = Resistor [tolerance=±5% resistance=4.7k package="0805 [SMD]"]

nets:
  N1: Mod1.pin1, Mod1.pin_10, Mod1.pin_26, LED1.anode, U1.GND, R1.Pin_1
  N2: Mod1.pin2, Mod1.pin_9, Mod1.pin_25, Mod1.pin_29, Q1.E, U1.VCC
  N3: Mod1.pin_11, U1.VOUT, R1.Pin_0
  N4: Mod1.pin_13, Q1.B
  N5: LED1.cathode, Q1.C
